# Fritzing sketch sensor-node (saved by Fritzing 0.8.3b)

parts:
  Bauteil1 = Arduino Pro Mini v13
  RHT1 = Humidity and Temperature Sensor RHT03
  Bauteil2 = Barometric Pressure Sensor - BMP180 Breakout (GY-68)
  U1 = CHJ-FST1000M [package=CHJ-FST1000M]
  R1 = Resistor [tolerance=±5% resistance=4.7k package="0603 [SMD]"]
  Bauteil3 = BH1750
  DS1 = DS18B20 1-Wire Temperature Sensor [part_number=DS18B20]
  DS2 = DS18B20 1-Wire Temperature Sensor [part_number=DS18B20]
  U2 = LIPO-110mAh [package=lipo-110]

nets:
  GND: Bauteil1.DTR, RHT1.GND_2, Bauteil2.GND, Bauteil3.GND
  VCC: Bauteil1.VCC, U1.+5V, U2.+
  GND_2: Bauteil1.GND, U1.GND, DS1.GND, DS2.GND, U2.-
  N1: Bauteil1.A4, Bauteil2.SDA, Bauteil3.SDA
  N2: Bauteil1.A5, Bauteil2.SCL, Bauteil3.SCL
  N3: Bauteil1.A3, U1.DATA
  N4: Bauteil1.A0, RHT1.Data-signal
  N5: Bauteil1.D13/SCK, RHT1.Vcc
  N6: Bauteil1.D7, Bauteil1.D6_PWM, R1.Pin_0, DS1.DQ, DS2.DQ
  VCC_2: Bauteil1.D5_PWM, Bauteil2.VCC, Bauteil3.VCC
  N7: Bauteil1.D4, R1.Pin_1

custom parts:
  CHJ-FST1000M: RF LINK
  BH1750: Light Sensor
