# Fritzing sketch window-switch (saved by Fritzing 0.8.3b)

parts:
  Bauteil1 = Arduino Pro Mini v13
  R2 = Resistor [tolerance=±5% resistance=1M package=THT]
  S1 = Pushbutton [package="[THT]"]

nets:
  N1: Bauteil1.VCC, S1.Pin_3
  N2: Bauteil1.GND, R2.Pin_0
  N3: Bauteil1.D2, R2.Pin_1, S1.Pin_1, S1.Pin_2
